# Fritzing sketch Arduino_Nano_nRF24L01 (saved by Fritzing 0.9.3b)

parts:
  Часть3 = Arduino Nano (Rev3.0) (ICSP)
  I2C_SSD1 = OLED 0.96" 128x64 I2C SSD1306
  Часть5 = NRF24L01+ Breakout Board

nets:
  N1: Часть3.D9, Часть5.CE
  N2: Часть3.D10, Часть5.CS
  N3: Часть3.D11/MOSI, Часть5.MOSI
  N4: Часть3.D12/MISO, Часть5.MISO
  GND: Часть3.GND, I2C_SSD1.GND, Часть5.GND
  N5: Часть3.A5, I2C_SSD1.SCL
  N6: Часть3.A4, I2C_SSD1.SCA
  VCC: Часть3.3V3, I2C_SSD1.VCC, Часть5.VCC
  N7: Часть3.D13/SCK, Часть5.SCK
