# Fritzing sketch Arduino_Nano_3oleds_ssd1306 (saved by Fritzing 0.9.3b)

parts:
  S1 = Taiway 100-SP-X-T1 SPDT Miniature Toggle Switch [part_number=100-SP-X-T1-0-0-B1-M1 package=THT]
  S2 = Taiway 100-SP-X-T1 SPDT Miniature Toggle Switch [part_number=100-SP-X-T1-0-0-B1-M1 package=THT]
  Power_plug1 = Power plug
  Часть3 = Arduino Nano (Rev3.0) (ICSP)
  CC1 = CC2500+PA+LNA
  I2C_SSD1 = OLED 0.96" 128x64 I2C SSD1306
  SPI_SSD1 = OLED 0.96" 128x64 SPI SSD1306
  SPI_SSD2 = OLED 0.96" 128x64 SPI SSD1306

nets:
  N1: S1.L1, Power_plug1.VCC
  N2: S1.L2, Часть3.5V
  GND: S2.L1, Power_plug1.GND, Часть3.GND, CC1.GND, CC1.PEN, I2C_SSD1.GND, SPI_SSD1.GND, SPI_SSD2.GND
  N3: S2.L2, Часть3.A3
  N4: Часть3.D3, SPI_SSD2.RES
  N5: Часть3.D4, SPI_SSD1.RES
  N6: Часть3.D5, SPI_SSD1.CLK, SPI_SSD2.CLK
  N7: Часть3.D6, SPI_SSD1.DIN, SPI_SSD2.DIN
  N8: Часть3.D7, SPI_SSD1.D/C, SPI_SSD2.D/C
  N9: Часть3.D8, SPI_SSD2.CS
  N10: Часть3.D9, SPI_SSD1.CS
  N11: Часть3.D10, CC1.CSN
  N12: Часть3.D11/MOSI, CC1.SI
  N13: Часть3.D12/MISO, CC1.SO
  N14: Часть3.A5, I2C_SSD1.SCL
  N15: Часть3.A4, I2C_SSD1.SCA
  VCC: Часть3.3V3, CC1.LEN, CC1.VCC, I2C_SSD1.VCC, SPI_SSD1.VCC, SPI_SSD2.VCC
  N16: Часть3.D13/SCK, CC1.SCLK

notes:
  Power
  Pause
  5V 50mA
