# Fritzing sketch ESP8266_oled_list_ssd1306 (saved by Fritzing 0.9.3b)

parts:
  Power_plug1 = Power plug
  IC1 = Voltage Regulator LM1117 [package=sot223]
  U1 = ESP8266 WiFi Module [part_number=ESP8266]
  Grove1 = Grove OLED 128x96

nets:
  GND: Power_plug1.GND, IC1.OUT, U1.GND, U1.TXD, Grove1.GND
  N1: Power_plug1.VCC, IC1.IN
  VCC: IC1.ADJ, U1.VCC, U1.CH_PD, Grove1.VCC
  N2: U1.GPIO_0, Grove1.SDA
  N3: U1.GPIO_2, Grove1.SCL

notes:
  5V 50mA
  3V3      5V

custom parts:
  ESP8266 WiFi Module: Generic WiFi Module based on the ESP8266 with onboard PCB antenna and UART communications
