# Fritzing sketch ESP8266_oled_spectrum_ssd1306 (saved by Fritzing 0.9.3b)

parts:
  Power_plug1 = Power plug
  I2C_SSD1 = OLED 0.96" 128x64 I2C SSD1306
  IC1 = Voltage Regulator LM1117 [package=sot223]
  U1 = ESP8266 WiFi Module [part_number=ESP8266]

nets:
  GND: Power_plug1.GND, I2C_SSD1.GND, IC1.OUT, U1.GND
  N1: Power_plug1.VCC, IC1.IN
  VCC: I2C_SSD1.VCC, IC1.ADJ, U1.RXD, U1.VCC, U1.RST, U1.CH_PD, U1.TXD
  N2: I2C_SSD1.SCL, U1.GPIO_2
  N3: I2C_SSD1.SCA, U1.GPIO_0

notes:
  5V 50mA
  3V3      5V

custom parts:
  ESP8266 WiFi Module: Generic WiFi Module based on the ESP8266 with onboard PCB antenna and UART communications
