# Fritzing sketch RPi_2oleds (saved by Fritzing 0.9.3b)

parts:
  Raspberry_Pi_1 = Raspberry Pi 3 [part_number=RPI-3-V1.2]
  I2C_SSD1 = OLED 0.96" 128x64 I2C SSD1306
  SPI_SSD1 = OLED 0.96" 128x64 SPI SSD1306
  Wixel1 = Wixel  # not connected

nets:
  3V3: Raspberry_Pi_1.3v3, Raspberry_Pi_1.3V3, I2C_SSD1.VCC, SPI_SSD1.VCC
  N1: Raspberry_Pi_1.GPIO2, I2C_SSD1.SCA
  N2: Raspberry_Pi_1.GPIO3, I2C_SSD1.SCL
  N3: Raspberry_Pi_1.GIPO10, SPI_SSD1.DIN
  N4: Raspberry_Pi_1.GIPO9, SPI_SSD1.D/C
  N5: Raspberry_Pi_1.GIPO11, SPI_SSD1.CLK
  GND: Raspberry_Pi_1.GND, I2C_SSD1.GND, SPI_SSD1.GND
  N6: Raspberry_Pi_1.GIPO8, SPI_SSD1.CS
  N7: Raspberry_Pi_1.GIPO25, SPI_SSD1.RES
